// Digital circuit CIS 310 Homework 1.4 1Bit Full Adder.dig as structural Verilog
module CIS_310_Homework_1_4_1Bit_Full_Adder (
  input  A,
  input  B,
  input  Cin,
  output Cout,
  output SUM
);

  wire and_1_out, and_2_out, xor_1_out;

  and and_1 (and_1_out, A, B);
  xor xor_1 (xor_1_out, A, B);
  and and_2 (and_2_out, xor_1_out, Cin);
  or or_1 (Cout, and_1_out, and_2_out);
  xor xor_2 (SUM, xor_1_out, Cin);
endmodule
