// Digital circuit CIS 310 Homework 1.5 4 Bit RippleCarry Adder.dig as structural Verilog
module CIS_310_Homework_1_5_4_Bit_RippleCarry_Adder (
  input  A0,
  input  B0,
  input  A1,
  input  B1,
  input  A2,
  input  B2,
  input  A3,
  input  B3,
  input  Cin,
  output S0,
  output S1,
  output S2,
  output S3,
  output Cout
);

  wire and_1_out, and_2_out, and_3_out, and_4_out, and_5_out, and_6_out, and_7_out, and_8_out, or_1_out,
       or_2_out, or_3_out, xor_1_out, xor_3_out, xor_5_out, xor_7_out;

  and and_1 (and_1_out, A0, B0);
  xor xor_1 (xor_1_out, A0, B0);
  and and_2 (and_2_out, xor_1_out, Cin);
  or or_1 (or_1_out, and_1_out, and_2_out);
  xor xor_2 (S0, xor_1_out, Cin);
  and and_3 (and_3_out, A1, B1);
  xor xor_3 (xor_3_out, A1, B1);
  and and_4 (and_4_out, xor_3_out, or_1_out);
  or or_2 (or_2_out, and_3_out, and_4_out);
  xor xor_4 (S1, xor_3_out, or_1_out);
  and and_5 (and_5_out, A2, B2);
  xor xor_5 (xor_5_out, A2, B2);
  and and_6 (and_6_out, xor_5_out, or_2_out);
  or or_3 (or_3_out, and_5_out, and_6_out);
  xor xor_6 (S2, xor_5_out, or_2_out);
  and and_7 (and_7_out, A3, B3);
  xor xor_7 (xor_7_out, A3, B3);
  and and_8 (and_8_out, xor_7_out, or_3_out);
  or or_4 (Cout, and_7_out, and_8_out);
  xor xor_8 (S3, xor_7_out, or_3_out);
endmodule
